// Logisim project XOR_3.circ as structural Verilog: 3 circuits, main circuit ALU_1_bit
module ALU_1_bit (
  input  CarryIn,
  input  A,
  input  Ainvert,
  input  [1:0] Op,
  input  B,
  input  Binvert,
  output Result,
  output CarryOut
);

  wire adder_1_out, and_1_out, and_2_out, and_3_out, multiplexer_1_out, multiplexer_2_out, multiplexer_3_out,
       not_1_out, not_2_out, not_3_out, not_4_out, or_1_out;

  not not_1 (not_1_out, A);
  Multiplexer multiplexer_1 (.in0(A), .in1(not_1_out), .out(multiplexer_1_out), .sel(Ainvert));
  Multiplexer multiplexer_2 (.in0(B), .in1(not_2_out), .out(multiplexer_2_out), .sel(Binvert));
  not not_2 (not_2_out, B);
  Adder #(.width(1)) adder_1 (
    .a(multiplexer_1_out), .b(multiplexer_2_out), .out(adder_1_out), .cin(CarryIn), .cout(CarryOut));
  not not_3 (not_3_out, A);
  not not_4 (not_4_out, B);
  and and_1 (and_1_out, multiplexer_1_out, multiplexer_2_out);
  or or_1 (or_1_out, multiplexer_1_out, multiplexer_2_out);
  and and_2 (and_2_out, not_3_out, B);
  and and_3 (and_3_out, A, not_4_out);
  Multiplexer multiplexer_3 (.in0(and_2_out), .in1(and_3_out), .out(multiplexer_3_out), .sel(A));
  Multiplexer #(.select(2)) multiplexer_4 (
    .in0(and_1_out), .in1(or_1_out), .in2(adder_1_out), .in3(multiplexer_3_out), .out(Result), .sel(Op));

  // Notes on the sheet:
  //   XOR
endmodule

module ALU_2_bit_test (
  input  Binvert,
  input  [1:0] Op,
  input  Ainvert,
  input  CarryIn,
  input  [1:0] in_5,
  input  [1:0] in_6,
  output [1:0] out_7,
  output CarryOut
);

  wire alu_1_bit_1_carryout;

  ALU_1_bit alu_1_bit_1 (
    .CarryIn(CarryIn), .A(in_5[0]), .Ainvert(Ainvert), .Op(Op), .B(in_6[0]), .Binvert(Binvert),
    .Result(out_7[0]), .CarryOut(alu_1_bit_1_carryout));
  ALU_1_bit alu_1_bit_2 (
    .CarryIn(alu_1_bit_1_carryout), .A(in_5[1]), .Ainvert(Ainvert), .Op(Op), .B(in_6[1]), .Binvert(Binvert),
    .Result(out_7[1]), .CarryOut(CarryOut));

  // Other names for the same wires on the sheet: A[1:0] = in_5; B[1:0] = in_6; Result[1:0] = out_7
endmodule

module ALU_1_bit_fix (
  input  CarryIn,
  input  A,
  input  Ainvert,
  input  [1:0] Op,
  input  B,
  input  Binvert,
  output Result,
  output CarryOut
);

  wire adder_1_out, and_1_out, and_2_out, multiplexer_1_out, multiplexer_2_out, not_1_out, not_2_out,
       not_3_out, or_1_out;

  not not_1 (not_1_out, A);
  Multiplexer multiplexer_1 (.in0(A), .in1(not_1_out), .out(multiplexer_1_out), .sel(Ainvert));
  Multiplexer multiplexer_2 (.in0(B), .in1(not_2_out), .out(multiplexer_2_out), .sel(Binvert));
  not not_2 (not_2_out, B);
  Adder #(.width(1)) adder_1 (
    .a(multiplexer_1_out), .b(multiplexer_2_out), .out(adder_1_out), .cin(CarryIn), .cout(CarryOut));
  and and_1 (and_1_out, multiplexer_1_out, multiplexer_2_out);
  or or_1 (or_1_out, multiplexer_1_out, multiplexer_2_out);
  not not_3 (not_3_out, and_1_out);
  and and_2 (and_2_out, not_3_out, adder_1_out);
  Multiplexer #(.select(2)) multiplexer_3 (
    .in0(and_1_out), .in1(or_1_out), .in2(adder_1_out), .in3(and_2_out), .out(Result), .sel(Op));
endmodule
