// Logisim project memlab.circ as structural Verilog: 4 circuits, main circuit main
module main (
  input  sweep_enable,
  output [9:0] out_2
);

  wire and_1_out, and_2_out, and_3_out, and_4_out, and_5_out, clk, comparator_1_gt, comparator_1_lt,
       comparator_2_eq, halt, mem_clear, mem_protect, multiplexer_1_out, not_1_out, not_2_out, not_3_out,
       not_4_out, read_mode, reset, rw_sel, undriven, write_mode, xor_1_out, xor_2_out;
  wire [3:0] hex_10_bit_display_1_lower, hex_10_bit_display_1_mid, hex_10_bit_display_1_upper;
  wire [7:0] firmware_1_data, onekram_1_rd, register_2_q;
  wire [9:0] adder_1_out;

  LED mem_fault (.in(not_1_out));
  Clock u_clk (.out(clk));
  Button u_reset (.out(reset));
  LED config_fault (.in(not_2_out));
  not not_1 (not_1_out, and_1_out);
  Comparator #(.width(10)) comparator_1 (
    .a(out_2), .b(10'hff), .gt(comparator_1_gt), .lt(comparator_1_lt));  // open: eq
  DipSwitch #(.number(3)) dipswitch_1 (.sw1(read_mode), .sw2(write_mode), .sw3(mem_protect));
  and and_1 (and_1_out, comparator_1_lt, write_mode, mem_protect);
  and and_2 (and_2_out, sweep_enable, clk);
  Button u_mem_clear (.out(mem_clear));
  not not_2 (not_2_out, and_5_out);
  Multiplexer multiplexer_1 (.in0(write_mode), .in1(comparator_1_gt), .out(multiplexer_1_out), .sel(mem_protect));
  and and_3 (and_3_out, sweep_enable, not_3_out);
  not not_3 (not_3_out, halt);
  xor xor_1 (xor_1_out, write_mode, read_mode);
  and and_4 (and_4_out, write_mode, read_mode);
  Register #(.width(10)) register_1 (.D(adder_1_out), .en(and_3_out), .clk(and_2_out), .Q(out_2), .clr(reset));
  not not_4 (not_4_out, xor_1_out);
  xor xor_2 (xor_2_out, multiplexer_1_out, read_mode);
  and and_5 (and_5_out, not_4_out, and_4_out);
  // NoConnect on undriven
  firmware firmware_1 (.addr(out_2), .data(firmware_1_data));
  Multiplexer multiplexer_2 (.in0(undriven), .in1(multiplexer_1_out), .out(rw_sel), .sel(xor_2_out));
  Adder #(.width(10)) adder_1 (.a(out_2), .b(10'h1), .out(adder_1_out));  // open: cin, cout
  Comparator comparator_2 (.a(firmware_1_data), .b({8{1'b0}}), .eq(comparator_2_eq));  // open: gt, lt
  Register register_2 (.D(firmware_1_data), .en(write_mode), .clk(clk), .Q(register_2_q));  // open: clr
  or or_1 (halt, comparator_2_eq, and_5_out);
  Hex_Digit_Display hex_digit_display_1 (.value(hex_10_bit_display_1_upper));  // open: dp
  hex_10_bit_display hex_10_bit_display_1 (
    .inp(out_2), .upper(hex_10_bit_display_1_upper), .mid(hex_10_bit_display_1_mid),
    .lower(hex_10_bit_display_1_lower));
  Hex_Digit_Display hex_digit_display_2 (.value(hex_10_bit_display_1_mid));  // open: dp
  Hex_Digit_Display hex_digit_display_3 (.value(hex_10_bit_display_1_lower));  // open: dp
  oneKram onekram_1 (.addr(out_2), .wd(register_2_q), .rw(rw_sel), .clk(clk), .clear(mem_clear), .rd(onekram_1_rd));
  Hex_Digit_Display hex_digit_display_4 (.value(onekram_1_rd[3:0]));  // open: dp
  Hex_Digit_Display hex_digit_display_5 (.value(onekram_1_rd[7:4]));  // open: dp

  // Other names for the same wires on the sheet: address[9:0] = out_2

  // Notes on the sheet:
  //   Memory Load/Read Sweep Control
  //   Configuration Switches
  //   Address
  //   Value
endmodule

module oneKram (
  input  [9:0] addr,
  input  [7:0] wd,
  input  rw,
  input  clk,
  input  clear,
  output [7:0] rd
);

  wire is_disabled, protected_read_write, rw_0, rw_1, rw_2, rw_3;
  wire [0:0] rw_e0, rw_e1, rw_e2, rw_e3;
  wire [7:0] multiplexer_1_out, ram_0, ram_1, ram_2, ram_3, undriven;

  RAM #(.asyncread("true"), .clearpin("true")) u_ram_1 (
    .addr(addr[7:0]), .we(rw_0), .oe(rw_e0[0]), .clk(clk), .din(wd), .dout(ram_0), .clr(clear));
  RAM #(.clearpin("true")) u_ram_2 (
    .addr(addr[7:0]), .we(rw_2), .oe(rw_e2[0]), .clk(clk), .din(wd), .dout(ram_2), .clr(clear));
  Demultiplexer #(.select(2)) demultiplexer_1 (
    .out0(rw_0), .out1(rw_1), .out2(rw_2), .out3(rw_3), .in(protected_read_write), .sel(addr[9:8]));
  RAM #(.clearpin("true")) u_ram_3 (
    .addr(addr[7:0]), .we(rw_1), .oe(rw_e1[0]), .clk(clk), .din(wd), .dout(ram_1), .clr(clear));
  RAM #(.clearpin("true")) ram_4 (
    .addr(addr[7:0]), .we(rw_3), .oe(rw_e3[0]), .clk(clk), .din(wd), .dout(ram_3), .clr(clear));
  Multiplexer #(.select(2), .width(8)) multiplexer_1 (
    .in0(ram_0), .in1(ram_1), .in2(ram_2), .in3(ram_3), .out(multiplexer_1_out), .sel(addr[9:8]));
  // NoConnect on undriven
  // Probe on rd
  Multiplexer #(.disabled("Z"), .width(8)) multiplexer_2 (
    .in0(multiplexer_1_out), .in1(undriven), .out(rd), .sel(is_disabled));
  Pull_Resistor pull_resistor_1 (.node(protected_read_write));
  buf buffer_1 (protected_read_write, rw);
  Pull_Resistor #(.pull(1)) pull_resistor_2 (.node(is_disabled));
  buf buffer_2 (is_disabled, rw);
  nor nor_1 (rw_e0[0], rw_0, is_disabled);
  nor nor_2 (rw_e1[0], rw_1, is_disabled);
  nor nor_3 (rw_e2[0], rw_2, is_disabled);
  nor nor_4 (rw_e3[0], rw_3, is_disabled);

  // Other names for the same wires on the sheet: address[9:0] = addr; bank_addr[7:0] = addr[7:0];
  //   chip_sel[1:0] = addr[9:8]; clock = clk; read_write = rw; rw_e0[1] = rw_0; rw_e1[1] = rw_1; rw_e2[1] = rw_2;
  //   rw_e3[1] = rw_3; write_data[7:0] = wd

  // Notes on the sheet:
  //   Inputs
  //   Memory Bank Management
  //   Outputs
  //   Read/Write Control For Floating Input
endmodule

module firmware (
  input  [9:0] addr,
  output [7:0] data
);

  ROM #(.addrWidth(10)) rom_1 (.addr(addr), .data(data));

  // Notes on the sheet:
  //   contents of rom_1 (hex, n*v repeats v):
  //   1 2 3 4 5 6 7 8 9 a b c d e f 10 11 12 13 14 15 16 17 18 19 1a 1b 1c 1d 1e 1f 20 21 22 23 24 25 26
  //   27 28 29 2a 2b 2c 2d 2e 2f 30 31 32 33 34 35 36 37 38 39 3a 3b 3c 3d 3e 3f 40 41 42 43 44 45 46 47
  //   48 49 4a 4b 4c 4d 4e 4f 50 51 52 53 54 55 56 57 58 59 5a 5b 5c 5d 5e 5f 60 61 62 63 64 65 66 67 68
  //   69 6a 6b 6c 6d 6e 6f 70 71 72 73 74 75 76 77 78 79 7a 7b 7c 7d 7e 7f 80 81 82 83 84 85 86 87 88 89
  //   8a 8b 8c 8d 8e 8f 90 91 92 93 94 95 96 97 98 99 9a 9b 9c 9d 9e 9f a0 a1 a2 a3 a4 a5 a6 a7 a8 a9 aa
  //   ab ac ad ae af b0 b1 b2 b3 b4 b5 b6 b7 b8 b9 ba bb bc bd be bf c0 c1 c2 c3 c4 c5 c6 c7 c8 c9 ca cb
  //   cc cd ce cf d0 d1 d2 d3 d4 d5 d6 d7 d8 d9 da db dc dd de df e0 e1 e2 e3 e4 e5 e6 e7 e8 e9 ea eb ec
  //   ed ee ef f0 f1 f2 f3 f4 f5 f6 f7 f8 f9 fa fb fc fd fe ff 1 2 3 4 5 6 7 8 9 a b c d e f 10 11 12 13
  //   14 15 16 17 18 19 1a 1b 1c 1d 1e 1f 20 21 22 23 24 25 26 27 28 29 2a 2b 2c 2d 2e 2f 30 31 32 33 34
  //   35 36 37 38 39 3a 3b 3c 3d 3e 3f 40 41 42 43 44 45 46 47 48 49 4a 4b 4c 4d 4e 4f 50 51 52 53 54 55
  //   56 57 58 59 5a 5b 5c 5d 5e 5f 60 61 62 63 64 65 66 67 68 69 6a 6b 6c 6d 6e 6f 70 71 72 73 74 75 76
  //   77 78 79 7a 7b 7c 7d 7e 7f 80 81 82 83 84 85 86 87 88 89 8a 8b 8c 8d 8e 8f 90 91 92 93 94 95 96 97
  //   98 99 9a 9b 9c 9d 9e 9f a0 a1 a2 a3 a4 a5 a6 a7 a8 a9 aa ab ac ad ae af b0 b1 b2 b3 b4 b5 b6 b7 b8
  //   b9 ba bb bc bd be bf c0 c1 c2 c3 c4 c5 c6 c7 c8 c9 ca cb cc cd ce cf d0 d1 d2 d3 d4 d5 d6 d7 d8 d9
  //   da db dc dd de df e0 e1 e2 e3 e4 e5 e6 e7 e8 e9 ea eb ec ed ee ef f0 f1 f2 f3 f4 f5 f6 f7 f8 f9 fa
  //   fb fc fd fe ff 1 2 3 4 5 6 7 8 9 a b c d e f 10 11 12 13 14 15 16 17 18 19 1a 1b 1c 1d 1e 1f 20 21
  //   22 23 24 25 26 27 28 29 2a 2b 2c 2d 2e 2f 30 31 32 33 34 35 36 37 38 39 3a 3b 3c 3d 3e 3f 40 41 42
  //   43 44 45 46 47 48 49 4a 4b 4c 4d 4e 4f 50 51 52 53 54 55 56 57 58 59 5a 5b 5c 5d 5e 5f 60 61 62 63
  //   64 65 66 67 68 69 6a 6b 6c 6d 6e 6f 70 71 72 73 74 75 76 77 78 79 7a 7b 7c 7d 7e 7f 80 81 82 83 84
  //   85 86 87 88 89 8a 8b 8c 8d 8e 8f 90 91 92 93 94 95 96 97 98 99 9a 9b 9c 9d 9e 9f a0 a1 a2 a3 a4 a5
  //   a6 a7 a8 a9 aa ab ac ad ae af b0 b1 b2 b3 b4 b5 b6 b7 b8 b9 ba bb bc bd be bf c0 c1 c2 c3 c4 c5 c6
  //   c7 c8 c9 ca cb cc cd ce cf d0 d1 d2 d3 d4 d5 d6 d7 d8 d9 da db dc dd de df e0 e1 e2 e3 e4 e5 e6 e7
  //   e8 e9 ea eb ec ed ee ef f0
endmodule

module hex_10_bit_display (
  input  [9:0] inp,
  output [3:0] mid,
  output [3:0] upper,
  output [3:0] lower
);


  assign lower = inp[3:0];
  assign mid = inp[7:4];
  assign upper = {2'b00, inp[9:8]};

  // Other names for the same wires on the sheet: upper_two[1:0] = inp[9:8]
endmodule
