// Logisim project Lab5.circ as structural Verilog
module FullAdder (
  input  a,
  input  b,
  input  c_in,
  output sum,
  output c_out
);

  wire and_1_out, and_2_out, xor_1_out;

  xor xor_1 (xor_1_out, a, b);
  and and_1 (and_1_out, xor_1_out, c_in);
  and and_2 (and_2_out, b, a);
  xor xor_2 (sum, xor_1_out, c_in);
  or or_1 (c_out, and_1_out, and_2_out);
endmodule

module FullAdder4Bit (
  input  [3:0] a,
  input  [3:0] b,
  input  in_3,
  output [3:0] sum,
  output out_5
);

  wire fulladder_1_c_out, fulladder_2_c_out, fulladder_3_c_out;

  FullAdder fulladder_1 (.a(a[0]), .b(b[0]), .c_in(in_3), .c_out(fulladder_1_c_out), .sum(sum[0]));
  FullAdder fulladder_2 (.a(a[1]), .b(b[1]), .c_in(fulladder_1_c_out), .c_out(fulladder_2_c_out), .sum(sum[1]));
  FullAdder fulladder_3 (.a(a[2]), .b(b[2]), .c_in(fulladder_2_c_out), .c_out(fulladder_3_c_out), .sum(sum[2]));
  FullAdder fulladder_4 (.a(a[3]), .b(b[3]), .c_in(fulladder_3_c_out), .c_out(out_5), .sum(sum[3]));

  // Other names for the same wires on the sheet: c_in = in_3; c_out = out_5; s0 = sum[0]; s1 = sum[1]; s2 = sum[2];
  //   s3 = sum[3]

  // Notes on the sheet:
  //   Inputs
  //   Outputs
endmodule

module FlipFlop (
);

  wire and_1_out, and_2_out, and_3_out, and_4_out, and_5_out, and_6_out, and_7_out, and_8_out, and_9_out,
       and_10_out, and_11_out, and_12_out, and_13_out, and_14_out, and_15_out, and_16_out, and_17_out,
       and_18_out, and_19_out, and_20_out, and_21_out, and_22_out, and_23_out, and_24_out, and_25_out,
       and_26_out, and_27_out, and_28_out, and_29_out, and_30_out, and_31_out, and_32_out, and_33_out,
       and_34_out, and_35_out, c_0, c_1, c_2, c_3, clock_1_out, d_ff_1_qn, d_ff_2_qn, d_ff_3_qn, d_ff_4_qn,
       not_1_out, not_2_out, not_3_out, not_4_out, or_1_out, or_2_out, or_3_out, or_4_out, or_5_out,
       or_6_out, or_7_out;

  Clock clock_1 (.out(clock_1_out));
  D_Flip_Flop d_ff_1 (.D(d_ff_1_qn), .clk(clock_1_out), .Q(c_0), .Qn(d_ff_1_qn));  // open: preset, reset
  D_Flip_Flop d_ff_2 (.D(d_ff_2_qn), .clk(d_ff_1_qn), .Q(c_1), .Qn(d_ff_2_qn));  // open: preset, reset
  D_Flip_Flop d_ff_3 (.D(d_ff_3_qn), .clk(d_ff_2_qn), .Q(c_2), .Qn(d_ff_3_qn));  // open: preset, reset
  D_Flip_Flop d_ff_4 (.D(d_ff_4_qn), .clk(d_ff_3_qn), .Q(c_3), .Qn(d_ff_4_qn));  // open: preset, reset
  not not_1 (not_1_out, c_3);
  not not_2 (not_2_out, c_2);
  not not_3 (not_3_out, c_1);
  not not_4 (not_4_out, c_0);
  and and_1 (and_1_out, not_2_out, not_4_out);
  and and_2 (and_2_out, not_1_out, c_1);
  and and_3 (and_3_out, not_1_out, c_2, c_0);
  and and_4 (and_4_out, c_3, not_2_out, not_3_out);
  and and_5 (and_5_out, c_3, not_4_out);
  and and_6 (and_6_out, c_2, c_1);
  and and_7 (and_7_out, not_1_out, not_3_out, not_4_out);
  and and_8 (and_8_out, not_1_out, c_1, c_0);
  and and_9 (and_9_out, not_2_out, not_4_out);
  and and_10 (and_10_out, c_3, not_3_out, c_0);
  and and_11 (and_11_out, not_1_out, not_2_out);
  and and_12 (and_12_out, not_1_out, c_2);
  and and_13 (and_13_out, c_3, not_2_out);
  and and_14 (and_14_out, not_3_out, c_0);
  and and_15 (and_15_out, not_2_out, not_3_out);
  and and_16 (and_16_out, not_2_out, c_0);
  and and_17 (and_17_out, c_2, not_3_out, c_0);
  and and_18 (and_18_out, not_1_out, not_2_out, not_4_out);
  and and_19 (and_19_out, not_2_out, c_1, c_0);
  and and_20 (and_20_out, c_3, not_3_out);
  and and_21 (and_21_out, c_2, c_1, not_4_out);
  and and_22 (and_22_out, not_2_out, not_4_out);
  and and_23 (and_23_out, c_1, not_4_out);
  and and_24 (and_24_out, c_3, c_1);
  and and_25 (and_25_out, c_3, c_2);
  and and_26 (and_26_out, not_3_out, not_4_out);
  and and_27 (and_27_out, not_1_out, c_2, not_3_out);
  and and_28 (and_28_out, c_2, not_4_out);
  and and_29 (and_29_out, c_3, not_2_out);
  and and_30 (and_30_out, c_3, c_1);
  and and_31 (and_31_out, not_2_out, c_1);
  and and_32 (and_32_out, c_3, not_2_out);
  and and_33 (and_33_out, not_1_out, c_2, not_3_out);
  and and_34 (and_34_out, c_1, not_4_out);
  and and_35 (and_35_out, c_3, c_0);
  or or_1 (or_1_out, and_1_out, and_2_out, and_3_out, and_4_out, and_5_out, and_6_out);
  or or_2 (or_2_out, and_7_out, and_8_out, and_9_out, and_10_out, and_11_out);
  or or_3 (or_3_out, and_12_out, and_13_out, and_14_out, and_15_out, and_16_out);
  or or_4 (or_4_out, and_17_out, and_18_out, and_19_out, and_20_out, and_21_out);
  or or_5 (or_5_out, and_22_out, and_23_out, and_24_out, and_25_out);
  or or_6 (or_6_out, and_26_out, and_27_out, and_28_out, and_29_out, and_30_out);
  or or_7 (or_7_out, and_31_out, and_32_out, and_33_out, and_34_out, and_35_out);
  _7_Segment_Display u_7_segment_display_1 (
    .g(or_7_out), .f(or_6_out), .a(or_1_out), .b(or_2_out), .e(or_5_out), .d(or_4_out), .c(or_3_out));  // open: dp
endmodule
