// Logisim project alu_starter.circ as structural Verilog: 8 circuits, main circuit main
module main (
  input  [3:0] in_1,
  input  [31:0] in_2,
  input  [31:0] in_3,
  input  [3:0] control,
  input  carry_in,
  input  [3:0] a,
  input  [3:0] b,
  output out_8,
  output [31:0] out_9,
  output out_10,
  output out_11,
  output [3:0] result,
  output carry_out
);

  wire alu_4_bit_1_set;

  alu_4_bit alu_4_bit_1 (
    .carry_in(carry_in), .a(a), .b(b), .control(control), .less_in(alu_4_bit_1_set), .alu_out(result),
    .set(alu_4_bit_1_set), .carry_out(carry_out), .zero(out_11));  // open: overflow
  alu_32_bit alu_32_bit_1 (
    .b(in_3), .a(in_2), .alu_op(in_1), .zero(out_8), .overflow(out_10), .result(out_9));  // open: carry_out

  // Notes on the sheet:
  //   TEST YOUR NEW 32-BIT ALU
endmodule

module alu_1_bit (
  input  a,
  input  b,
  input  Carry_in,
  input  less,
  input  [3:0] ALU_op,
  output ALU_out,
  output Carry_out
);

  wire adder_1_out, and_1_out, multiplexer_1_out, multiplexer_2_out, not_1_out, not_2_out, or_1_out;

  not not_1 (not_1_out, a);
  not not_2 (not_2_out, b);
  Multiplexer multiplexer_1 (.in0(a), .in1(not_1_out), .out(multiplexer_1_out), .sel(ALU_op[3]));
  Multiplexer multiplexer_2 (.in0(b), .in1(not_2_out), .out(multiplexer_2_out), .sel(ALU_op[2]));
  and and_1 (and_1_out, multiplexer_1_out, multiplexer_2_out);
  or or_1 (or_1_out, multiplexer_1_out, multiplexer_2_out);
  Adder #(.width(1)) adder_1 (
    .a(multiplexer_1_out), .b(multiplexer_2_out), .out(adder_1_out), .cin(Carry_in), .cout(Carry_out));
  Multiplexer #(.select(2)) multiplexer_3 (
    .in0(and_1_out), .in1(or_1_out), .in2(adder_1_out), .in3(less), .out(ALU_out), .sel(ALU_op[1:0]));

  // Other names for the same wires on the sheet: alu_sel[1:0] = ALU_op[1:0]; b_inv = ALU_op[2]; a_inv = ALU_op[3]

  // Notes on the sheet:
  //   ALU Cell
endmodule

module alu_1_bit_set_overflow (
  input  a,
  input  b,
  input  Carry_in,
  input  less,
  input  [3:0] ALU_op,
  output ALU_out,
  output set,
  output overflow,
  output Carry_out
);

  wire adder_1_out, and_1_out, multiplexer_1_out, multiplexer_2_out, not_1_out, not_2_out, or_1_out;

  Multiplexer multiplexer_1 (.in0(a), .in1(not_1_out), .out(multiplexer_1_out), .sel(ALU_op[3]));
  not not_1 (not_1_out, a);
  Multiplexer multiplexer_2 (.in0(b), .in1(not_2_out), .out(multiplexer_2_out), .sel(ALU_op[2]));
  not not_2 (not_2_out, b);
  and and_1 (and_1_out, multiplexer_1_out, multiplexer_2_out);
  or or_1 (or_1_out, multiplexer_1_out, multiplexer_2_out);
  Adder #(.width(1)) adder_1 (
    .a(multiplexer_1_out), .b(multiplexer_2_out), .out(adder_1_out), .cin(Carry_in), .cout(Carry_out));
  Multiplexer #(.select(2)) multiplexer_3 (
    .in0(and_1_out), .in1(or_1_out), .in2(adder_1_out), .in3(less), .out(ALU_out), .sel(ALU_op[1:0]));
  xor xor_1 (overflow, Carry_out, Carry_in);
  xor xor_2 (set, adder_1_out, overflow);

  // Other names for the same wires on the sheet: alu_sel[1:0] = ALU_op[1:0]; b_inv = ALU_op[2]; a_inv = ALU_op[3]

  // Notes on the sheet:
  //   ALU Bit
  //   (w/overflow)
  //   used for sign bit in ALU
endmodule

module alu_4_bit (
  input  less_in,
  input  carry_in,
  input  [3:0] a,
  input  [3:0] b,
  input  [3:0] control,
  output zero,
  output [3:0] alu_out,
  output set,
  output overflow,
  output carry_out
);

  wire alu_1_bit_1_carry_out, alu_1_bit_2_carry_out, alu_1_bit_3_carry_out, or_1_out;

  alu_1_bit alu_1_bit_1 (
    .a(a[0]), .b(b[0]), .less(less_in), .ALU_op(control), .Carry_in(carry_in),
    .Carry_out(alu_1_bit_1_carry_out), .ALU_out(alu_out[0]));
  alu_1_bit alu_1_bit_2 (
    .a(a[1]), .b(b[1]), .less(1'b0), .ALU_op(control), .Carry_in(alu_1_bit_1_carry_out),
    .Carry_out(alu_1_bit_2_carry_out), .ALU_out(alu_out[1]));
  alu_1_bit alu_1_bit_3 (
    .a(a[2]), .b(b[2]), .less(1'b0), .ALU_op(control), .Carry_in(alu_1_bit_2_carry_out),
    .Carry_out(alu_1_bit_3_carry_out), .ALU_out(alu_out[2]));
  alu_1_bit_set_overflow alu_1_bit_set_overflow_1 (
    .ALU_op(control), .a(a[3]), .b(b[3]), .less(1'b0), .Carry_in(alu_1_bit_3_carry_out),
    .Carry_out(carry_out), .ALU_out(alu_out[3]), .set(set), .overflow(overflow));
  // Probe on alu_out
  or or_1 (or_1_out, alu_out[0], alu_out[1], alu_out[2], alu_out[3]);
  not not_1 (zero, or_1_out);

  // Other names for the same wires on the sheet: c_in = carry_in; l_in = less_in; op[3:0] = control

  // Notes on the sheet:
  //   control
  //   0 0 0 0
  //   0 0 0 1
  //   0 0 1 0
  //   0 1 1 0
  //   0 1 1 1
  //   function
  //   and
  //   or
  //   add
  //   sub (c_in = 1)
  //   slt (c_in = 1)
endmodule

module alu_32_bit (
  input  [31:0] a,
  input  [31:0] b,
  input  [3:0] alu_op,
  output [31:0] result,
  output zero,
  output carry_out,
  output overflow
);

  wire alu_4_bit_1_carry_out, alu_4_bit_1_overflow, alu_4_bit_1_set, alu_4_bit_2_carry_out,
       alu_4_bit_2_overflow, alu_4_bit_2_set, alu_4_bit_3_carry_out, alu_4_bit_3_overflow, alu_4_bit_3_set,
       alu_4_bit_4_carry_out, alu_4_bit_4_overflow, alu_4_bit_4_set, alu_4_bit_5_carry_out,
       alu_4_bit_5_overflow, alu_4_bit_5_set, alu_4_bit_6_carry_out, alu_4_bit_6_overflow, alu_4_bit_6_set,
       alu_4_bit_7_carry_out, alu_4_bit_7_overflow, alu_4_bit_7_set, SETout, z0, z1, z2, z3, z4, z5, z6, z7;

  // NoConnect on {alu_op[3], alu_op[1:0]}
  alu_4_bit alu_4_bit_1 (
    .carry_in(alu_op[2]), .a(a[3:0]), .b(b[3:0]), .control(alu_op), .less_in(SETout), .alu_out(result[3:0]),
    .set(alu_4_bit_1_set), .overflow(alu_4_bit_1_overflow), .carry_out(alu_4_bit_1_carry_out), .zero(z0));
  // NoConnect on alu_4_bit_1_overflow
  // NoConnect on alu_4_bit_1_set
  alu_4_bit alu_4_bit_2 (
    .carry_in(alu_4_bit_1_carry_out), .a(a[7:4]), .b(b[7:4]), .control(alu_op), .less_in(1'b0),
    .alu_out(result[7:4]), .set(alu_4_bit_2_set), .overflow(alu_4_bit_2_overflow),
    .carry_out(alu_4_bit_2_carry_out), .zero(z1));
  // NoConnect on alu_4_bit_2_overflow
  // NoConnect on alu_4_bit_2_set
  alu_4_bit alu_4_bit_3 (
    .carry_in(alu_4_bit_2_carry_out), .a(a[11:8]), .b(b[11:8]), .control(alu_op), .less_in(1'b0),
    .alu_out(result[11:8]), .set(alu_4_bit_3_set), .overflow(alu_4_bit_3_overflow),
    .carry_out(alu_4_bit_3_carry_out), .zero(z2));
  // NoConnect on alu_4_bit_3_overflow
  // NoConnect on alu_4_bit_3_set
  alu_4_bit alu_4_bit_4 (
    .carry_in(alu_4_bit_3_carry_out), .a(a[15:12]), .b(b[15:12]), .control(alu_op), .less_in(1'b0),
    .alu_out(result[15:12]), .set(alu_4_bit_4_set), .overflow(alu_4_bit_4_overflow),
    .carry_out(alu_4_bit_4_carry_out), .zero(z3));
  // NoConnect on alu_4_bit_4_overflow
  // NoConnect on alu_4_bit_4_set
  alu_4_bit alu_4_bit_5 (
    .carry_in(alu_4_bit_4_carry_out), .a(a[19:16]), .b(b[19:16]), .control(alu_op), .less_in(1'b0),
    .alu_out(result[19:16]), .set(alu_4_bit_5_set), .overflow(alu_4_bit_5_overflow),
    .carry_out(alu_4_bit_5_carry_out), .zero(z4));
  alu_4_bit alu_4_bit_6 (
    .carry_in(alu_4_bit_5_carry_out), .a(a[23:20]), .b(b[23:20]), .control(alu_op), .less_in(1'b0),
    .alu_out(result[23:20]), .set(alu_4_bit_6_set), .overflow(alu_4_bit_6_overflow),
    .carry_out(alu_4_bit_6_carry_out), .zero(z5));
  alu_4_bit alu_4_bit_7 (
    .carry_in(alu_4_bit_6_carry_out), .a(a[27:24]), .b(b[27:24]), .control(alu_op), .less_in(1'b0),
    .alu_out(result[27:24]), .set(alu_4_bit_7_set), .overflow(alu_4_bit_7_overflow),
    .carry_out(alu_4_bit_7_carry_out), .zero(z6));
  alu_4_bit alu_4_bit_8 (
    .carry_in(alu_4_bit_7_carry_out), .a(a[31:28]), .b(b[31:28]), .control(alu_op), .less_in(1'b0),
    .alu_out(result[31:28]), .set(SETout), .overflow(overflow), .carry_out(carry_out), .zero(z7));
  // NoConnect on alu_4_bit_5_overflow
  // NoConnect on alu_4_bit_5_set
  // NoConnect on alu_4_bit_6_overflow
  // NoConnect on alu_4_bit_6_set
  // NoConnect on alu_4_bit_7_overflow
  // NoConnect on alu_4_bit_7_set
  and and_1 (zero, z0, z1, z2, z3, z4, z5, z6, z7);

  // Other names for the same wires on the sheet: a0[3:0] = a[3:0]; a1[3:0] = a[7:4]; a2[3:0] = a[11:8];
  //   a3[3:0] = a[15:12]; a4[3:0] = a[19:16]; a5[3:0] = a[23:20]; a6[3:0] = a[27:24]; a7[3:0] = a[31:28];
  //   alu_out[31:0] = result; r0[3:0] = result[3:0]; r1[3:0] = result[7:4]; r2[3:0] = result[11:8];
  //   r3[3:0] = result[15:12]; r4[3:0] = result[19:16]; r5[3:0] = result[23:20]; r6[3:0] = result[27:24];
  //   r7[3:0] = result[31:28]; b0[3:0] = b[3:0]; b1[3:0] = b[7:4]; b2[3:0] = b[11:8]; b3[3:0] = b[15:12];
  //   b4[3:0] = b[19:16]; b5[3:0] = b[23:20]; b6[3:0] = b[27:24]; b7[3:0] = b[31:28]; control[3:0] = alu_op;
  //   c_in = alu_op[2]; Cout = carry_out; ZERO_alu = zero

  // Notes on the sheet:
  //   0 0 0 0
  //   0 0 0 1
  //   0 0 1 0
  //   0 1 1 0
  //   0 1 1 1
  //   1 1 0 0
  //   1 1 0 1
  //   Inputs
  //   Outputs
  //   control
  //   and
  //   or
  //   add
  //   sub
  //   slt
  //   nor
  //   nand
  //   function
endmodule

module test_1_bit (
);

  wire alu_1_bit_1_alu_out, alu_1_bit_1_carry_out, alu_1_bit_2_alu_out, alu_1_bit_2_carry_out,
       alu_1_bit_3_alu_out, alu_1_bit_3_carry_out, alu_1_bit_4_alu_out, alu_1_bit_4_carry_out,
       alu_1_bit_5_alu_out, alu_1_bit_5_carry_out, alu_1_bit_6_alu_out, alu_1_bit_6_carry_out,
       alu_1_bit_7_alu_out, alu_1_bit_7_carry_out, alu_1_bit_8_alu_out, alu_1_bit_8_carry_out,
       alu_1_bit_9_alu_out, alu_1_bit_9_carry_out, alu_1_bit_10_alu_out, alu_1_bit_10_carry_out,
       alu_1_bit_11_alu_out, alu_1_bit_11_carry_out, alu_1_bit_12_alu_out, alu_1_bit_12_carry_out;

  alu_1_bit alu_1_bit_1 (
    .a(1'b0), .b(1'b0), .ALU_op(4'b0000), .Carry_in(1'b0), .Carry_out(alu_1_bit_1_carry_out),
    .ALU_out(alu_1_bit_1_alu_out));  // open: less
  // Probe on alu_1_bit_2_alu_out
  alu_1_bit alu_1_bit_2 (
    .a(1'b0), .b(1'b0), .ALU_op(4'b0001), .Carry_in(1'b0), .Carry_out(alu_1_bit_2_carry_out),
    .ALU_out(alu_1_bit_2_alu_out));  // open: less
  // Probe on alu_1_bit_2_carry_out
  // Probe on alu_1_bit_3_alu_out
  alu_1_bit alu_1_bit_3 (
    .a(1'b0), .b(1'b0), .ALU_op(4'b0010), .Carry_in(1'b0), .Carry_out(alu_1_bit_3_carry_out),
    .ALU_out(alu_1_bit_3_alu_out));  // open: less
  // Probe on alu_1_bit_3_carry_out
  // Probe on alu_1_bit_4_alu_out
  alu_1_bit alu_1_bit_4 (
    .a(1'b0), .b(1'b0), .ALU_op(4'b0010), .Carry_in(1'b1), .Carry_out(alu_1_bit_4_carry_out),
    .ALU_out(alu_1_bit_4_alu_out));  // open: less
  // Probe on alu_1_bit_4_carry_out
  // Probe on alu_1_bit_1_alu_out
  // Probe on alu_1_bit_1_carry_out
  // Probe on alu_1_bit_5_alu_out
  alu_1_bit alu_1_bit_5 (
    .a(1'b1), .b(1'b0), .ALU_op(4'b0000), .Carry_in(1'b0), .Carry_out(alu_1_bit_5_carry_out),
    .ALU_out(alu_1_bit_5_alu_out));  // open: less
  // Probe on alu_1_bit_5_carry_out
  // Probe on alu_1_bit_6_alu_out
  alu_1_bit alu_1_bit_6 (
    .a(1'b0), .b(1'b1), .ALU_op(4'b0001), .Carry_in(1'b0), .Carry_out(alu_1_bit_6_carry_out),
    .ALU_out(alu_1_bit_6_alu_out));  // open: less
  // Probe on alu_1_bit_6_carry_out
  // Probe on alu_1_bit_7_alu_out
  alu_1_bit alu_1_bit_7 (
    .a(1'b0), .b(1'b1), .ALU_op(4'b0010), .Carry_in(1'b0), .Carry_out(alu_1_bit_7_carry_out),
    .ALU_out(alu_1_bit_7_alu_out));  // open: less
  // Probe on alu_1_bit_7_carry_out
  // Probe on alu_1_bit_8_alu_out
  alu_1_bit alu_1_bit_8 (
    .a(1'b0), .b(1'b1), .ALU_op(4'b0010), .Carry_in(1'b1), .Carry_out(alu_1_bit_8_carry_out),
    .ALU_out(alu_1_bit_8_alu_out));  // open: less
  // Probe on alu_1_bit_8_carry_out
  // Probe on alu_1_bit_9_alu_out
  alu_1_bit alu_1_bit_9 (
    .a(1'b1), .b(1'b1), .ALU_op(4'b0000), .Carry_in(1'b0), .Carry_out(alu_1_bit_9_carry_out),
    .ALU_out(alu_1_bit_9_alu_out));  // open: less
  // Probe on alu_1_bit_9_carry_out
  // Probe on alu_1_bit_10_alu_out
  alu_1_bit alu_1_bit_10 (
    .a(1'b1), .b(1'b1), .ALU_op(4'b0001), .Carry_in(1'b0), .Carry_out(alu_1_bit_10_carry_out),
    .ALU_out(alu_1_bit_10_alu_out));  // open: less
  // Probe on alu_1_bit_10_carry_out
  // Probe on alu_1_bit_11_alu_out
  alu_1_bit alu_1_bit_11 (
    .a(1'b1), .b(1'b1), .ALU_op(4'b0010), .Carry_in(1'b0), .Carry_out(alu_1_bit_11_carry_out),
    .ALU_out(alu_1_bit_11_alu_out));  // open: less
  // Probe on alu_1_bit_11_carry_out
  // Probe on alu_1_bit_12_alu_out
  alu_1_bit alu_1_bit_12 (
    .a(1'b1), .b(1'b1), .ALU_op(4'b0010), .Carry_in(1'b1), .Carry_out(alu_1_bit_12_carry_out),
    .ALU_out(alu_1_bit_12_alu_out));  // open: less
  // Probe on alu_1_bit_12_carry_out

  // Notes on the sheet:
  //   AND Tests
  //   OR Tests
  //   ADD Tests
endmodule

module test_4_bit (
);

  wire alu_4_bit_1_carry_out, alu_4_bit_1_overflow, alu_4_bit_1_zero, alu_4_bit_2_carry_out,
       alu_4_bit_2_overflow, alu_4_bit_2_zero, alu_4_bit_3_carry_out, alu_4_bit_3_overflow, alu_4_bit_3_zero,
       alu_4_bit_4_carry_out, alu_4_bit_4_overflow, alu_4_bit_4_zero, alu_4_bit_5_carry_out,
       alu_4_bit_5_overflow, alu_4_bit_5_zero, alu_4_bit_6_carry_out, alu_4_bit_6_overflow, alu_4_bit_6_zero,
       alu_4_bit_7_carry_out, alu_4_bit_7_overflow, alu_4_bit_7_zero, alu_4_bit_8_carry_out,
       alu_4_bit_8_overflow, alu_4_bit_8_zero, alu_4_bit_9_carry_out, alu_4_bit_9_overflow, alu_4_bit_9_zero,
       alu_4_bit_10_carry_out, alu_4_bit_10_overflow, alu_4_bit_10_zero, alu_4_bit_11_carry_out,
       alu_4_bit_11_overflow, alu_4_bit_11_zero, s1, s2, s3, s4, s5, s6, s7, s8, s9, s10;
  wire [3:0] alu_4_bit_1_alu_out, alu_4_bit_2_alu_out, alu_4_bit_3_alu_out, alu_4_bit_4_alu_out,
       alu_4_bit_5_alu_out, alu_4_bit_6_alu_out, alu_4_bit_7_alu_out, alu_4_bit_8_alu_out,
       alu_4_bit_9_alu_out, alu_4_bit_10_alu_out, alu_4_bit_11_alu_out;

  // Probe on alu_4_bit_1_zero
  // Probe on alu_4_bit_1_alu_out
  alu_4_bit alu_4_bit_1 (
    .a(4'b1010), .b(4'b1111), .control(4'b0000), .less_in(s1), .alu_out(alu_4_bit_1_alu_out), .set(s1),
    .overflow(alu_4_bit_1_overflow), .carry_out(alu_4_bit_1_carry_out), .zero(alu_4_bit_1_zero));  // open: carry_in
  // Probe on alu_4_bit_1_overflow
  // Probe on alu_4_bit_1_carry_out
  // Probe on alu_4_bit_2_zero
  // Probe on alu_4_bit_2_alu_out
  alu_4_bit alu_4_bit_2 (
    .carry_in(1'b1), .a(4'b0101), .b(4'b0011), .control(4'b0110), .less_in(s5),
    .alu_out(alu_4_bit_2_alu_out), .set(s5), .overflow(alu_4_bit_2_overflow),
    .carry_out(alu_4_bit_2_carry_out), .zero(alu_4_bit_2_zero));
  // Probe on alu_4_bit_2_overflow
  // Probe on alu_4_bit_2_carry_out
  // Probe on alu_4_bit_3_zero
  // Probe on alu_4_bit_3_alu_out
  alu_4_bit alu_4_bit_3 (
    .carry_in(1'b1), .a(4'b0100), .b(4'b0100), .control(4'b0111), .less_in(s9),
    .alu_out(alu_4_bit_3_alu_out), .set(s9), .overflow(alu_4_bit_3_overflow),
    .carry_out(alu_4_bit_3_carry_out), .zero(alu_4_bit_3_zero));
  // Probe on alu_4_bit_3_overflow
  // Probe on alu_4_bit_3_carry_out
  alu_4_bit alu_4_bit_4 (
    .carry_in(1'b1), .a(4'b0011), .b(4'b0101), .control(4'b0110), .less_in(s6),
    .alu_out(alu_4_bit_4_alu_out), .set(s6), .overflow(alu_4_bit_4_overflow),
    .carry_out(alu_4_bit_4_carry_out), .zero(alu_4_bit_4_zero));
  // Probe on alu_4_bit_5_zero
  // Probe on alu_4_bit_5_alu_out
  alu_4_bit alu_4_bit_5 (
    .a(4'b1010), .b(4'b1111), .control(4'b0001), .less_in(s2), .alu_out(alu_4_bit_5_alu_out), .set(s2),
    .overflow(alu_4_bit_5_overflow), .carry_out(alu_4_bit_5_carry_out), .zero(alu_4_bit_5_zero));  // open: carry_in
  // Probe on alu_4_bit_5_overflow
  // Probe on alu_4_bit_5_carry_out
  // Probe on alu_4_bit_4_zero
  // Probe on alu_4_bit_4_alu_out
  // Probe on alu_4_bit_4_overflow
  // Probe on alu_4_bit_4_carry_out
  // Probe on alu_4_bit_6_zero
  // Probe on alu_4_bit_6_alu_out
  alu_4_bit alu_4_bit_6 (
    .carry_in(1'b1), .a(4'b0100), .b(4'b0101), .control(4'b0110), .less_in(s10),
    .alu_out(alu_4_bit_6_alu_out), .set(s10), .overflow(alu_4_bit_6_overflow),
    .carry_out(alu_4_bit_6_carry_out), .zero(alu_4_bit_6_zero));
  // Probe on alu_4_bit_6_overflow
  // Probe on alu_4_bit_6_carry_out
  alu_4_bit alu_4_bit_7 (
    .a(4'b0011), .b(4'b0100), .control(4'b0010), .less_in(s3), .alu_out(alu_4_bit_7_alu_out), .set(s3),
    .overflow(alu_4_bit_7_overflow), .carry_out(alu_4_bit_7_carry_out), .zero(alu_4_bit_7_zero));  // open: carry_in
  alu_4_bit alu_4_bit_8 (
    .carry_in(1'b1), .a(4'b0011), .b(4'b0100), .control(4'b0111), .less_in(s7),
    .alu_out(alu_4_bit_8_alu_out), .set(s7), .overflow(alu_4_bit_8_overflow),
    .carry_out(alu_4_bit_8_carry_out), .zero(alu_4_bit_8_zero));
  // Probe on alu_4_bit_7_zero
  // Probe on alu_4_bit_7_alu_out
  // Probe on alu_4_bit_7_overflow
  // Probe on alu_4_bit_7_carry_out
  // Probe on alu_4_bit_8_zero
  // Probe on alu_4_bit_8_alu_out
  // Probe on alu_4_bit_8_overflow
  // Probe on alu_4_bit_8_carry_out
  // Probe on alu_4_bit_9_zero
  // Probe on alu_4_bit_9_alu_out
  alu_4_bit alu_4_bit_9 (
    .carry_in(1'b1), .a(4'b0100), .b(4'b0100), .control(4'b0111), .less_in(s9),
    .alu_out(alu_4_bit_9_alu_out), .set(s9), .overflow(alu_4_bit_9_overflow),
    .carry_out(alu_4_bit_9_carry_out), .zero(alu_4_bit_9_zero));
  // Probe on alu_4_bit_9_overflow
  // Probe on alu_4_bit_9_carry_out
  // Probe on alu_4_bit_10_zero
  // Probe on alu_4_bit_10_alu_out
  alu_4_bit alu_4_bit_10 (
    .a(4'b0100), .b(4'b0110), .control(4'b0010), .less_in(s4), .alu_out(alu_4_bit_10_alu_out), .set(s4),
    .overflow(alu_4_bit_10_overflow), .carry_out(alu_4_bit_10_carry_out), .zero(alu_4_bit_10_zero));  // open: carry_in
  // Probe on alu_4_bit_10_overflow
  // Probe on alu_4_bit_10_carry_out
  // Probe on alu_4_bit_11_zero
  // Probe on alu_4_bit_11_alu_out
  alu_4_bit alu_4_bit_11 (
    .carry_in(1'b1), .a(4'b0100), .b(4'b0011), .control(4'b0111), .less_in(s8),
    .alu_out(alu_4_bit_11_alu_out), .set(s8), .overflow(alu_4_bit_11_overflow),
    .carry_out(alu_4_bit_11_carry_out), .zero(alu_4_bit_11_zero));
  // Probe on alu_4_bit_11_overflow
  // Probe on alu_4_bit_11_carry_out

  // Notes on the sheet:
  //   AND
  //   SUB
  //   SLT-False-Equal
  //   OR
  //   SUB Negative
  //   Zero-False
  //   SUM
  //   SLT-True
  //   Zero-True
  //   SUM w/ Overflow
  //   SLT-False
endmodule

module test_32_bit (
  output out_1,
  output out_2,
  output out_3,
  output [31:0] out_4,
  output [31:0] out_5,
  output [31:0] out_6,
  output out_7,
  output out_8,
  output out_9,
  output out_10,
  output out_11,
  output out_12,
  output out_13,
  output out_14,
  output out_15,
  output [31:0] out_16,
  output [31:0] out_17,
  output [31:0] out_18,
  output out_19,
  output out_20,
  output out_21,
  output out_22,
  output out_23,
  output out_24,
  output out_25,
  output out_26,
  output out_27,
  output [31:0] out_28,
  output [31:0] out_29,
  output [31:0] out_30,
  output out_31,
  output out_32,
  output out_33,
  output out_34,
  output out_35,
  output out_36,
  output out_37,
  output out_38,
  output out_39,
  output [31:0] out_40,
  output [31:0] out_41,
  output [31:0] out_42,
  output out_43,
  output out_44,
  output out_45,
  output out_46,
  output out_47,
  output out_48,
  output out_49,
  output out_50,
  output out_51,
  output [31:0] out_52,
  output [31:0] out_53,
  output [31:0] out_54,
  output out_55,
  output out_56,
  output out_57,
  output out_58,
  output out_59,
  output out_60
);

  alu_32_bit alu_32_bit_1 (
    .b(32'h6), .a(32'h2d), .alu_op(4'b0010), .zero(out_1), .carry_out(out_10), .overflow(out_7),
    .result(out_4));
  alu_32_bit alu_32_bit_2 (
    .b({32{1'b1}}), .a(32'hfffffffe), .alu_op(4'b0010), .zero(out_14), .carry_out(out_23), .overflow(out_20),
    .result(out_17));
  alu_32_bit alu_32_bit_3 (
    .b(32'h11), .a(32'h1), .alu_op(4'b0000), .zero(out_49), .carry_out(out_58), .overflow(out_55),
    .result(out_52));
  alu_32_bit alu_32_bit_4 (
    .b(32'h6), .a(32'h5), .alu_op(4'b0111), .zero(out_25), .carry_out(out_34), .overflow(out_31),
    .result(out_28));
  alu_32_bit alu_32_bit_5 (
    .b(32'h6), .a(32'hfffffffe), .alu_op(4'b0111), .zero(out_37), .carry_out(out_46), .overflow(out_43),
    .result(out_40));
  alu_32_bit alu_32_bit_6 (
    .b(32'h6), .a(32'h7), .alu_op(4'b0110), .zero(out_2), .carry_out(out_11), .overflow(out_8), .result(out_5));
  alu_32_bit alu_32_bit_7 (
    .b(32'h5), .a(32'hfffffffe), .alu_op(4'b0110), .zero(out_13), .carry_out(out_22), .overflow(out_19),
    .result(out_16));
  alu_32_bit alu_32_bit_8 (
    .b(32'h5), .a(32'h5), .alu_op(4'b0111), .zero(out_26), .carry_out(out_35), .overflow(out_32),
    .result(out_29));
  alu_32_bit alu_32_bit_9 (
    .b(32'h6), .a(32'h7fffffff), .alu_op(4'b0010), .zero(out_38), .carry_out(out_47), .overflow(out_44),
    .result(out_41));
  alu_32_bit alu_32_bit_10 (
    .b(32'h6), .a(32'h80000001), .alu_op(4'b0110), .zero(out_50), .carry_out(out_59), .overflow(out_56),
    .result(out_53));
  alu_32_bit alu_32_bit_11 (
    .b({32{1'b1}}), .a({32{1'b1}}), .alu_op(4'b0000), .zero(out_3), .carry_out(out_12), .overflow(out_9),
    .result(out_6));
  alu_32_bit alu_32_bit_12 (
    .b(32'h1), .a({32{1'b0}}), .alu_op(4'b0001), .zero(out_15), .carry_out(out_24), .overflow(out_21),
    .result(out_18));
  alu_32_bit alu_32_bit_13 (
    .b({32{1'b0}}), .a(32'h1), .alu_op(4'b1100), .zero(out_27), .carry_out(out_36), .overflow(out_33),
    .result(out_30));
  alu_32_bit alu_32_bit_14 (
    .b({32{1'b0}}), .a(32'h1), .alu_op(4'b1101), .zero(out_39), .carry_out(out_48), .overflow(out_45),
    .result(out_42));
  alu_32_bit alu_32_bit_15 (
    .b({32{1'b0}}), .a({32{1'b0}}), .alu_op(4'b0000), .zero(out_51), .carry_out(out_60), .overflow(out_57),
    .result(out_54));

  // Notes on the sheet:
  //   Zero False
  //   ADD
  //   ADD Negative a, b
  //   a < b
  //   a < b, -a
  //   SUB
  //   SUB Negative a, b
  //   a >= b
  //   Overflow Positive
  //   Overflow Negative
  //   AND
  //   OR
  //   NOR
  //   NAND
  //   Zero True
endmodule
